// Logisim project CPUFinal.circ as structural Verilog: 19 circuits, main circuit main
module main (
  output [15:0] out_1,
  output [4:0] out_2,
  output [7:0] out_3,
  output [15:0] out_4,
  output [15:0] out_5,
  output [15:0] out_6,
  output [4:0] out_7,
  output [1:0] out_8,
  output [2:0] out_9,
  output [2:0] out_10,
  output [2:0] out_11
);

  wire and_1_out, and_2_out, blebnehandler_1_out_4, clock_1_out, control_1_out_2, control_1_out_3,
       control_1_out_5, control_1_out_7, control_1_out_8, control_1_out_9, control_1_out_10,
       control_1_out_11, control_1_out_12, control_1_out_13, control_1_out_14, not_1_out;
  wire [2:0] demultiplexer_1_out1;
  wire [10:8] rom_1_data;
  wire [15:0] adder_1_out, adder_2_out, bit_extender_1_out, multiplexer_1_out, multiplexer_2_out,
       multiplexer_3_out, multiplexer_4_out, multiplexer_5_out, PC_q, RA_q, ram_1_dout, register_1_q;

  Register #(.width(16)) register_1 (
    .D(adder_2_out), .en(control_1_out_14), .clk(and_1_out), .Q(register_1_q));  // open: clr
  Register #(.trigger("falling"), .width(16)) RA (.D(register_1_q), .en(1'b1), .clk(and_1_out), .Q(RA_q));  // open: clr
  Multiplexer #(.enable("false"), .width(16)) multiplexer_1 (
    .in0(adder_2_out), .in1(adder_1_out), .out(multiplexer_1_out), .sel(control_1_out_10));
  Multiplexer #(.enable("false"), .width(16)) multiplexer_2 (
    .in0(multiplexer_1_out), .in1(RA_q), .out(multiplexer_2_out), .sel(control_1_out_11));
  not not_1 (not_1_out, control_1_out_7);
  and and_1 (and_1_out, not_1_out, clock_1_out);
  Clock clock_1 (.out(clock_1_out));
  Register #(.width(16)) PC (.D(multiplexer_2_out), .en(1'b1), .clk(and_1_out), .Q(PC_q));  // open: clr
  Adder #(.width(16)) adder_1 (.a(out_1), .b(PC_q), .out(adder_1_out));  // open: cin, cout
  Multiplexer #(.enable("false"), .width(16)) multiplexer_3 (
    .in0(16'h1), .in1(bit_extender_1_out), .out(multiplexer_3_out), .sel(and_2_out));
  ROM #(.addrWidth(16), .dataWidth(16)) rom_1 (.addr(PC_q), .data({out_2, rom_1_data, out_3}));
  Adder #(.width(16)) adder_2 (.a(multiplexer_3_out), .b(PC_q), .out(adder_2_out));  // open: cin, cout
  assign bit_extender_1_out = {{13{demultiplexer_1_out1[2]}}, demultiplexer_1_out1};  // Bit_Extender bit_extender_1
  Demultiplexer #(.enable("false"), .width(3)) demultiplexer_1 (
    .out0(out_11), .out1(demultiplexer_1_out1), .in(rom_1_data), .sel(control_1_out_12));
  assign out_1 = {{11{out_3[4]}}, out_3[4:0]};  // Bit_Extender bit_extender_2
  Control control_1 (
    .in_1(out_2), .out_2(control_1_out_2), .out_3(control_1_out_3), .out_5(control_1_out_5), .out_6(out_8),
    .out_7(control_1_out_7), .out_8(control_1_out_8), .out_9(control_1_out_9), .out_10(control_1_out_10),
    .out_11(control_1_out_11), .out_12(control_1_out_12), .out_13(control_1_out_13), .out_14(control_1_out_14));  // open: out_4
  RegisterFile2 registerfile2_1 (
    .out_8(out_5), .out_9(out_4), .readreg2(out_3[7:5]), .readreg1(out_3[4:2]), .writeregister(out_11),
    .write(control_1_out_2), .Registerdata(multiplexer_5_out), .clock(and_1_out));  // open: reset
  Multiplexer #(.enable("false"), .width(16)) multiplexer_4 (
    .in0(out_4), .in1(out_1), .out(multiplexer_4_out), .sel(control_1_out_3));
  BleBneHandler blebnehandler_1 (.out_4(blebnehandler_1_out_4), .in_1(out_5), .in_2(out_4), .in_3(control_1_out_13));
  and and_2 (and_2_out, control_1_out_12, blebnehandler_1_out_4);
  ALU alu_1 (.out_4(out_6), .in_1(multiplexer_4_out), .in_2(out_5), .in_3(out_8));
  RAM #(.addrWidth(16), .dataWidth(16), .trigger("falling")) ram_1 (
    .addr(out_4), .we(control_1_out_9), .oe(control_1_out_8), .clk(and_1_out), .din(out_5), .dout(ram_1_dout));
  Multiplexer #(.enable("false"), .width(16)) multiplexer_5 (
    .in0(out_6), .in1(ram_1_dout), .out(multiplexer_5_out), .sel(control_1_out_5));

  assign out_7 = out_3[4:0];
  assign out_9 = out_3[7:5];
  assign out_10 = out_3[4:2];

  // Notes on the sheet:
  //   contents of rom_1 (hex, n*v repeats v):
  //   6 104 d007 6340 7 108 d003 6440 c003 1204 e000 f000 168*0 1 102 212 1104 a728 f000
endmodule

module ALU (
  input  [15:0] in_1,
  input  [15:0] in_2,
  input  [1:0] in_3,
  output [15:0] out_4
);

  wire [15:0] adder_1_out, and_1_out, or_1_out;

  Adder #(.width(16)) adder_1 (.a(in_1), .b(in_2), .out(adder_1_out));  // open: cin, cout
  assign and_1_out = in_1 & in_2;  // AND_Gate and_1, 16 bits wide
  assign or_1_out = in_1 | in_2;  // OR_Gate or_1, 16 bits wide
  Multiplexer #(.enable("false"), .select(2), .width(16)) multiplexer_1 (
    .in0(in_1), .in1(adder_1_out), .in2(and_1_out), .in3(or_1_out), .out(out_4), .sel(in_3));
endmodule

module Control (
  input  [4:0] in_1,
  output out_2,
  output out_3,
  output out_4,
  output out_5,
  output [1:0] out_6,
  output out_7,
  output out_8,
  output out_9,
  output out_10,
  output out_11,
  output out_12,
  output out_13,
  output out_14
);

  // ALUOPP aluopp_1: pin names not known; wires that end beside it: in_1, out_6[0], out_6[1]
  // RegWrite regwrite_1: pin names not known; wires that end beside it: in_1, out_2
  // ALUUSrc aluusrc_1: pin names not known; wires that end beside it: in_1, out_3
  // RegDst regdst_1: pin names not known; wires that end beside it: in_1, out_4
  // MemToReg memtoreg_1: pin names not known; wires that end beside it: in_1, out_5
  // ClockStop clockstop_1: pin names not known; wires that end beside it: in_1, out_7
  // MemRead memread_1: pin names not known; wires that end beside it: in_1, out_8
  // MemWrite memwrite_1: pin names not known; wires that end beside it: in_1, out_9
  // Jump jump_1: pin names not known; wires that end beside it: in_1, out_10
  // Rtn rtn_1: pin names not known; wires that end beside it: in_1, out_11
  // branchouttt branchouttt_1: pin names not known; wires that end beside it: in_1, out_12
  // beqble beqble_1: pin names not known; wires that end beside it: in_1, out_13
  // call call_1: pin names not known; wires that end beside it: in_1, out_14
endmodule

module BleBneHandler (
  input  [15:0] in_1,
  input  [15:0] in_2,
  input  in_3,
  output out_4
);

  wire and_1_out, comparator_1_eq, comparator_1_lt, not_1_out;

  Comparator #(.mode("unsigned"), .width(16)) comparator_1 (
    .a(in_1), .b(in_2), .eq(comparator_1_eq), .lt(comparator_1_lt));  // open: gt
  not not_1 (not_1_out, comparator_1_eq);
  and and_1 (and_1_out, comparator_1_eq, comparator_1_lt);
  Multiplexer #(.enable("false")) multiplexer_1 (.in0(not_1_out), .in1(and_1_out), .out(out_4), .sel(in_3));
endmodule

module ControlUnit2 (
  input  [4:0] in_1,
  output out_2,
  output out_3,
  output out_4,
  output out_5,
  output [1:0] out_6,
  output out_7,
  output out_8,
  output out_9,
  output out_10,
  output out_11,
  output out_12,
  output out_13,
  output out_14
);

  RegWrite2 regwrite2_1 (.in_1(in_1), .out_2(out_2));
  AluSrc2 alusrc2_1 (.in_1(in_1), .out_2(out_3));
  RegDst2 regdst2_1 (.in_1(in_1), .out_2(out_4));
  MemToReg2 memtoreg2_1 (.in_1(in_1), .out_2(out_5));
  AluOp2 aluop2_1 (.in_1(in_1), .out_2(out_6[0]), .out_3(out_6[1]));
  ClockStop2 clockstop2_1 (.in_1(in_1), .out_2(out_7));
  MemRead2 memread2_1 (.in_1(in_1), .out_2(out_8));
  MemWrite2 memwrite2_1 (.in_1(in_1), .out_2(out_9));
  Jump2 jump2_1 (.in_1(in_1), .out_2(out_10));
  Rtn2 rtn2_1 (.in_1(in_1), .out_2(out_11));
  BranchOut branchout_1 (.in_1(in_1), .out_2(out_12));
  BeqBle2 beqble2_1 (.in_1(in_1), .out_2(out_13));
  Call2 call2_1 (.in_1(in_1), .out_2(out_14));
endmodule

module AluOp2 (
  input  [4:0] in_1,
  output out_2,
  output out_3
);

  wire and_1_out, and_2_out, and_3_out, and_4_out, and_5_out, and_6_out, not_1_out, not_2_out, not_3_out,
       not_4_out, not_5_out;

  not not_1 (not_1_out, in_1[4]);
  not not_2 (not_2_out, in_1[2]);
  not not_3 (not_3_out, in_1[1]);
  not not_4 (not_4_out, in_1[3]);
  not not_5 (not_5_out, in_1[3]);
  and and_1 (and_1_out, not_1_out, in_1[3], in_1[2], in_1[1]);
  and and_2 (and_2_out, not_1_out, not_4_out, in_1[1]);
  and and_3 (and_3_out, not_1_out, in_1[3], not_2_out, not_3_out);
  and and_4 (and_4_out, in_1[4], not_5_out, not_2_out, in_1[1]);
  and and_5 (and_5_out, not_1_out, not_5_out, in_1[2]);
  and and_6 (and_6_out, in_1[4], not_5_out, not_2_out);
  or or_1 (out_2, and_1_out, and_2_out, and_3_out, and_4_out);
  or or_2 (out_3, and_5_out, and_6_out);
endmodule

module BeqBle2 (
  input  [4:0] in_1,
  output out_2
);


  assign out_2 = in_1[1];
endmodule

module Call2 (
  input  [4:0] in_1,
  output out_2
);

  wire not_1_out;

  not not_1 (not_1_out, in_1[2]);
  and and_1 (out_2, in_1[4], in_1[3], not_1_out, in_1[1]);
endmodule

module BranchOut (
  input  [4:0] in_1,
  output out_2
);

  wire not_1_out;

  not not_1 (not_1_out, in_1[3]);
  and and_1 (out_2, in_1[4], not_1_out, in_1[2]);
endmodule

module Rtn2 (
  input  [4:0] in_1,
  output out_2
);

  wire not_1_out;

  not not_1 (not_1_out, in_1[1]);
  and and_1 (out_2, not_1_out, in_1[2], in_1[3], in_1[4]);
endmodule

module AluSrc2 (
  input  [4:0] in_1,
  output out_2
);

  wire and_1_out, and_2_out, and_3_out, not_1_out, not_2_out, not_3_out, not_4_out, not_5_out, not_6_out;

  not not_1 (not_1_out, in_1[1]);
  not not_2 (not_2_out, in_1[2]);
  not not_3 (not_3_out, in_1[4]);
  not not_4 (not_4_out, in_1[4]);
  not not_5 (not_5_out, in_1[3]);
  not not_6 (not_6_out, in_1[2]);
  and and_1 (and_1_out, not_1_out, not_2_out, not_3_out);
  and and_2 (and_2_out, not_4_out, in_1[3], in_1[1]);
  and and_3 (and_3_out, not_5_out, in_1[4], not_6_out);
  or or_1 (out_2, and_1_out, and_2_out, and_3_out);
endmodule

module RegWrite2 (
  input  [4:0] in_1,
  output out_2
);

  wire and_1_out, and_2_out, and_3_out, and_4_out, not_1_out, not_2_out, not_3_out, not_4_out, not_5_out,
       not_6_out;

  not not_1 (not_1_out, in_1[4]);
  not not_2 (not_2_out, in_1[3]);
  not not_3 (not_3_out, in_1[2]);
  not not_4 (not_4_out, in_1[3]);
  and and_1 (and_1_out, not_4_out, not_1_out);
  and and_2 (and_2_out, not_1_out, in_1[2]);
  not not_5 (not_5_out, in_1[2]);
  and and_3 (and_3_out, not_5_out, not_1_out, not_6_out);
  not not_6 (not_6_out, in_1[1]);
  and and_4 (and_4_out, in_1[4], not_2_out, not_3_out);
  or or_1 (out_2, and_4_out, and_1_out, and_2_out, and_3_out);
endmodule

module RegDst2 (
  input  [4:0] in_1,
  output out_2
);

  wire and_1_out, and_2_out, not_1_out, not_2_out, not_3_out;

  not not_1 (not_1_out, in_1[4]);
  not not_2 (not_2_out, in_1[3]);
  not not_3 (not_3_out, not_2_out);
  and and_1 (and_1_out, not_1_out, not_2_out, in_1[1]);
  and and_2 (and_2_out, not_2_out, in_1[2], not_3_out);
  or or_1 (out_2, and_1_out, and_2_out);
endmodule

module MemWrite2 (
  input  [4:0] in_1,
  output out_2
);

  wire not_1_out, not_2_out;

  not not_1 (not_1_out, in_1[2]);
  not not_2 (not_2_out, in_1[4]);
  and and_1 (out_2, in_1[1], not_1_out, in_1[3], not_2_out);
endmodule

module MemToReg2 (
  input  [4:0] in_1,
  output out_2
);

  wire not_1_out, not_2_out;

  not not_1 (not_1_out, in_1[2]);
  not not_2 (not_2_out, in_1[4]);
  and and_1 (out_2, in_1[1], not_1_out, in_1[3], not_2_out);
endmodule

module MemRead2 (
  input  [4:0] in_1,
  output out_2
);

  wire not_1_out, not_2_out, not_3_out;

  not not_1 (not_1_out, in_1[1]);
  not not_2 (not_2_out, in_1[2]);
  not not_3 (not_3_out, in_1[4]);
  and and_1 (out_2, not_1_out, not_2_out, in_1[3], not_3_out);
endmodule

module ClockStop2 (
  input  [4:0] in_1,
  output out_2
);

  and and_1 (out_2, in_1[1], in_1[2], in_1[3], in_1[4]);
endmodule

module RegisterFile2 (
  input  write,
  input  [2:0] writeregister,
  input  [2:0] readreg2,
  input  [2:0] readreg1,
  input  [15:0] Registerdata,
  input  clock,
  input  reset,
  output [15:0] out_8,
  output [15:0] out_9
);

  wire and_1_out, and_2_out, and_3_out, and_4_out, and_5_out, and_6_out, and_7_out, and_8_out,
       decoder_1_out0, decoder_1_out1, decoder_1_out2, decoder_1_out3, decoder_1_out4, decoder_1_out5,
       decoder_1_out6, decoder_1_out7;
  wire [15:0] register_1_q, register_2_q, register_3_q, register_4_q, register_5_q, register_6_q,
       register_7_q, register_8_q;

  Decoder #(.select(3)) decoder_1 (
    .out0(decoder_1_out0), .out1(decoder_1_out1), .out2(decoder_1_out2), .out3(decoder_1_out3),
    .out4(decoder_1_out4), .out5(decoder_1_out5), .out6(decoder_1_out6), .out7(decoder_1_out7),
    .sel(writeregister));  // open: en
  and and_1 (and_1_out, write, decoder_1_out0);
  and and_2 (and_2_out, write, decoder_1_out1);
  and and_3 (and_3_out, write, decoder_1_out2);
  and and_4 (and_4_out, write, decoder_1_out3);
  and and_5 (and_5_out, write, decoder_1_out4);
  and and_6 (and_6_out, write, decoder_1_out5);
  and and_7 (and_7_out, write, decoder_1_out6);
  and and_8 (and_8_out, write, decoder_1_out7);
  Register #(.width(16)) register_1 (.D(Registerdata), .en(and_1_out), .clk(clock), .Q(register_1_q), .clr(reset));
  Register #(.width(16)) register_2 (.D(Registerdata), .en(and_2_out), .clk(clock), .Q(register_2_q), .clr(reset));
  Register #(.width(16)) register_3 (.D(Registerdata), .en(and_3_out), .clk(clock), .Q(register_3_q), .clr(reset));
  Register #(.width(16)) register_4 (.D(Registerdata), .en(and_4_out), .clk(clock), .Q(register_4_q), .clr(reset));
  Register #(.width(16)) register_5 (.D(Registerdata), .en(and_5_out), .clk(clock), .Q(register_5_q));  // open: clr
  Register #(.width(16)) register_6 (.D(Registerdata), .en(and_6_out), .clk(clock), .Q(register_6_q), .clr(reset));
  Register #(.width(16)) register_7 (.D(Registerdata), .en(and_7_out), .clk(clock), .Q(register_7_q), .clr(reset));
  Register #(.width(16)) register_8 (.D(Registerdata), .en(and_8_out), .clk(clock), .Q(register_8_q), .clr(reset));
  Multiplexer #(.enable("false"), .select(3), .width(16)) multiplexer_1 (
    .in0(register_1_q), .in1(register_2_q), .in2(register_3_q), .in3(register_4_q), .in4(register_5_q),
    .in5(register_6_q), .in6(register_7_q), .in7(register_8_q), .out(out_8), .sel(readreg1));
  Multiplexer #(.enable("false"), .select(3), .width(16)) multiplexer_2 (
    .in0(register_1_q), .in1(register_2_q), .in2(register_3_q), .in3(register_4_q), .in4(register_5_q),
    .in5(register_6_q), .in6(register_7_q), .in7(register_8_q), .out(out_9), .sel(readreg2));
endmodule

module Jump2 (
  input  [4:0] in_1,
  output out_2
);

  wire not_1_out;

  not not_1 (not_1_out, in_1[2]);
  and and_1 (out_2, in_1[4], in_1[3], not_1_out);
endmodule
